// Digital circuit 16bitRegister.dig as structural Verilog
module _16bitRegister (
  input  [7:0] DB,
  input  nLDL,
  input  nLDH,
  input  INC,
  input  CLK,
  input  nOE,
  output [15:0] MB,
  output [15:0] val
);

  wire HIGH_0_p4, HIGH_0_p12, LOW_0_p12;
  wire [3:0] id_H, id_L;

  // _74245 DB_LOW: pin names not known; wires that end beside it: 1'b1, 1'b1, 1'b0, DB[0], DB[1], DB[2], DB[3], DB[4], DB[5], DB[6], DB[7], nLDL, id_L[0], id_L[1], id_L[2], id_L[3], id_H[0], id_H[1], id_H[2], id_H[3]
  // _74245 DB_HIGH: pin names not known; wires that end beside it: 1'b1, 1'b1, 1'b0, DB[0], DB[1], DB[2], DB[3], DB[4], DB[5], DB[6], DB[7], nLDH, id_L[0], id_L[1], id_L[2], id_L[3], id_H[0], id_H[1], id_H[2], id_H[3]
  PullUp #(.Bits(4)) pullup_1 (.out(id_L));
  PullUp #(.Bits(4)) pullup_2 (.out(id_H));
  // _74161 LOW_0: pin names not known; wires that end beside it: nLDL, 1'b1, CLK, 1'b1, INC, id_L[0], id_L[1], id_L[2], id_L[3], 1'b1, 1'b0, LOW_0_p12, val[0], val[1], val[2], val[3]
  // _74161 HIGH_0: pin names not known; wires that end beside it: nLDH, 1'b1, CLK, HIGH_0_p4, INC, id_L[0], id_L[1], id_L[2], id_L[3], 1'b1, 1'b0, HIGH_0_p12, val[8], val[9], val[10], val[11]
  // _74161 LOW_1: pin names not known; wires that end beside it: nLDL, 1'b1, CLK, LOW_0_p12, INC, id_H[0], id_H[1], id_H[2], id_H[3], 1'b1, 1'b0, HIGH_0_p4, val[4], val[5], val[6], val[7]
  // _74161 HIGH_1: pin names not known; wires that end beside it: nLDH, 1'b1, CLK, HIGH_0_p12, INC, id_H[0], id_H[1], id_H[2], id_H[3], 1'b1, 1'b0, val[12], val[13], val[14], val[15]
  // _74245 MB_LOW: pin names not known; wires that end beside it: 1'b1, 1'b1, 1'b0, val[0], val[1], val[2], val[3], val[4], val[5], val[6], val[7], nOE, MB[0], MB[1], MB[2], MB[3], MB[4], MB[5], MB[6], MB[7]
  // _74245 MB_HIGH: pin names not known; wires that end beside it: 1'b1, 1'b1, 1'b0, val[8], val[9], val[10], val[11], val[12], val[13], val[14], val[15], nOE, MB[8], MB[9], MB[10], MB[11], MB[12], MB[13], MB[14], MB[15]

  // Other names for the same wires on the sheet: imb_0[3:0] = val[3:0]; imb_2[3:0] = val[11:8]; imb_1[3:0] = val[7:4];
  //   imb_3[3:0] = val[15:12]; LDH = nLDH; LDL = nLDL; OE = nOE

  // Notes on the sheet:
  //   Inputs:
  //   - Data Bus
  //   - Load Low Byte
  //   - Load High Byte
  //   - Increment Value
  //   - Output Enable
  //   - Clock
  //   Outputs:
  //   - Assert to Memory Bus
  //   - Debugging value out
endmodule
