// Digital circuit j8ger_cpu.dig as structural Verilog
module j8ger_cpu (
  input  clk
);

  wire d_ff_1_nq, d_ff_1_q, DOWN_out, multiplexer_1_out, RIGHT_out;

  Button RIGHT (.out(RIGHT_out));
  Multiplexer multiplexer_1 (.sel(d_ff_1_q), .in_0(RIGHT_out), .in_1(clk), .out(multiplexer_1_out));
  D_FF d_ff_1 (.D(d_ff_1_nq), .C(DOWN_out), .Q(d_ff_1_q), .nQ(d_ff_1_nq));
  Button DOWN (.out(DOWN_out));
  DataRegisters dataregisters_1 ();  // open: D_LBE, D_RBE, D_WE, DB, CLK, LHB, RHB, X, Y, A, T
endmodule
